# Fritzing sketch light_sensor (saved by Fritzing 0.9.2b)
breadboards: 1

parts:
  Componente1 = Arduino Uno (Rev3)
  R1 = Resistor [tolerance=±5% resistance=220 package=THT]
  R2 = Resistor [tolerance=±5% resistance=220 package=THT]
  R3 = Resistor [tolerance=±5% resistance=220 package=THT]
  R4 = Resistor [tolerance=±5% resistance=1k package=THT]
  LED1 = LED - 5mm [color="Red (633nm)" package="5 mm [THT]"]
  LED2 = LED - 5mm [color="Yellow (592nm)" package="5 mm [THT]"]
  LED3 = LED - 5mm [color="Green (560nm)" package="5 mm [THT]"]
  R5 = Photocell (LDR) [package=THT]

nets:
  N1: Componente1.A0, R4.Pin_1, R5.pin_1
  N2: Componente1.D8, LED1.anode
  N3: Componente1.D9_PWM, LED2.anode
  N4: Componente1.D10_PWM/SS, LED3.anode
  N5: Componente1.GND, R1.Pin_0, R2.Pin_0, R3.Pin_0, R4.Pin_0
  N6: Componente1.5V, R5.pin_0
  N7: R1.Pin_1, LED3.cathode
  N8: R2.Pin_1, LED2.cathode
  N9: R3.Pin_1, LED1.cathode
