# Fritzing sketch light-translator (saved by Fritzing 0.9.2b)
breadboards: 1

parts:
  Componente1 = Arduino Uno (Rev3)
  R1 = Photocell (LDR) [package=THT]
  R2 = Resistor [tolerance=±5% resistance=220 package=THT]
  R3 = Resistor [tolerance=±5% resistance=220 package=THT]
  LED1 = LED - 5mm [color="Red (633nm)" package="5 mm [THT]"]

nets:
  N1: Componente1.A5/SCL, R1.pin_1, R2.Pin_0
  N2: Componente1.D3_PWM, LED1.anode
  N3: Componente1.3V3, R1.pin_0
  N4: Componente1.GND, R2.Pin_1, R3.Pin_0
  N5: R3.Pin_1, LED1.cathode
