# Fritzing sketch pto_acesso (saved by Fritzing 0.9.2b)
breadboards: 1

parts:
  Componente1 = Arduino Uno (Rev3)
  R1 = Dial Potentiometer with switch
  R2 = Resistor [tolerance=±5% resistance=220 package=THT]
  R3 = Resistor [tolerance=±5% resistance=220 package=THT]

nets:
  N1: Componente1.GND, R2.Pin_1, R3.Pin_1
  N2: Componente1.D2, R1.leg2
  N3: Componente1.D3_PWM, R1.wiper
  N4: Componente1.5V, R1.leg1
