# Fritzing sketch circuit (saved by Fritzing 0.9.2b)
breadboards: 1

parts:
  Componente1 = Arduino Nano (Rev3.0)
  R1 = Resistor [tolerance=±5% resistance=1k package=THT]
  R3 = Resistor [tolerance=±5% resistance=1k package=THT]
  R4 = Resistor [tolerance=±5% resistance=1k package=THT]
  R5 = Resistor [tolerance=±5% resistance=1k package=THT]
  R8 = Resistor [tolerance=±5% resistance=1k package=THT]
  T1 = LM35 Temperature Sensor [package="TO92 [THT]"]
  R9 = Photocell (LDR) [package=THT]
  R10 = Resistor [tolerance=±5% resistance=1k package=THT]

nets:
  GND: Componente1.GND, R8.Pin_1, T1.GND, R9.pin_0
  N1: Componente1.5V, R1.Pin_0, R10.Pin_1
  N2: Componente1.A1, R9.pin_1, R10.Pin_0
  N3: Componente1.A0, T1.Vout
  N4: R1.Pin_1, R3.Pin_0
  N5: R3.Pin_1, R4.Pin_0
  N6: R4.Pin_1, R5.Pin_0
  N7: R5.Pin_1, R8.Pin_0, T1.+Vs
