# Fritzing sketch simple_key (saved by Fritzing 0.9.2b)
breadboards: 1

parts:
  Componente1 = Arduino Uno (Rev3)
  S1 = Pushbutton [package=THT]
  J1 = Piezo Speaker
  R1 = Resistor [tolerance=±5% resistance=470 package=THT]
  R2 = Resistor [tolerance=±5% resistance=100 package=THT]
  R3 = Resistor [tolerance=±5% resistance=100 package=THT]
  R4 = Resistor [tolerance=±5% resistance=100 package=THT]
  R5 = Resistor [tolerance=±5% resistance=470 package=THT]
  R6 = Resistor [tolerance=±5% resistance=470 package=THT]  # not connected
  R7 = Resistor [tolerance=±5% resistance=470 package=THT]
  S3 = Pushbutton [package=THT]
  S4 = Pushbutton [package=THT]

nets:
  N1: Componente1.D8, S1.leg1, R7.Pin_0
  N2: Componente1.D10_PWM/SS, S4.leg1
  N3: Componente1.D12/MISO, R5.Pin_0, S3.leg1
  N4: Componente1.D3_PWM, J1.pin2
  N5: Componente1.5V, R2.Pin_1, R3.Pin_1, R4.Pin_1
  N6: Componente1.GND, R1.Pin_0, R5.Pin_1, R7.Pin_1
  N7: S1.leg0, R3.Pin_0
  N8: J1.pin1, R1.Pin_1
  N9: R2.Pin_0, S3.leg0
  N10: R4.Pin_0, S4.leg0

// code stored in the sketch: simple_key.ino
const int BUZZER = 3;
const int NO_BUTTONS = 3;
const int BUTTON[] = {8, 10, 12};
const float FREQ[] = {440, 587.33, 659.25};

void setup() {
  pinMode(BUZZER, OUTPUT);
  for (int i = 0; i < NO_BUTTONS; ++i)
    pinMode(BUTTON[i], INPUT);
}

void loop() {
  float freq = -1;

  for (int i = 0; i < NO_BUTTONS; ++i)
    if (digitalRead(BUTTON[i]) == HIGH)
      freq = FREQ[i];

  if (freq > 0)
    tone(BUZZER, freq, 5);
}
