# Fritzing sketch washroom (saved by Fritzing 0.9.2b)
breadboards: 1

parts:
  Componente1 = Arduino Uno (Rev3)
  R1 = Resistor [tolerance=±5% resistance=10k package=THT]
  R2 = Photocell (LDR) [package=THT]
  LED1 = LED - 5mm [color="Red (633nm)" package="5 mm [THT]"]
  J1 = Infrared Proximity Sensor

nets:
  N1: Componente1.A0, R1.Pin_0, R2.pin_1
  GND: Componente1.GND, R2.pin_0, LED1.cathode, J1.GND
  N2: Componente1.D3_PWM, J1.Vout
  N3: Componente1.D5_PWM, LED1.anode
  5V: Componente1.5V, R1.Pin_1, J1.Vcc
