# Fritzing sketch whack (saved by Fritzing 0.9.2b)
breadboards: 1

parts:
  Componente1 = Arduino Uno (Rev3)
  S1 = Pushbutton [package=THT]
  S2 = Pushbutton [package=THT]
  R1 = Resistor [tolerance=±10% resistance=470 package=THT]
  R2 = Resistor [tolerance=±5% resistance=470 package=THT]
  R3 = Resistor [tolerance=±5% resistance=470 package=THT]
  R4 = Resistor [tolerance=±5% resistance=470 package=THT]
  LED1 = LED - 5mm [color="Red (633nm)" package="5 mm [THT]"]
  LED2 = LED - 5mm [color="Red (633nm)" package="5 mm [THT]"]

nets:
  N1: Componente1.D8, R3.Pin_1, LED1.cathode, LED1.anode
  N2: Componente1.D9_PWM, R4.Pin_1, LED2.cathode, LED2.anode
  N3: Componente1.D2, S1.leg1, R1.Pin_1
  N4: Componente1.D3_PWM, S2.leg1, R2.Pin_1
  N5: Componente1.5V, S1.leg0, S2.leg0
  N6: Componente1.GND, R1.Pin_0, R3.Pin_0, R4.Pin_0
